// Digital circuit CORE.dig as structural Verilog
module CORE (
  input  clk,
  input  RST,
  input  CLR,
  input  in_4
);

  wire ALUD_CO, ALUDH_OE, ALUDL_OE, ALUS_OE, and_3_out, ASSERT_f, BR_Q, button_1_out, CLK_t, CLKR,
       comparator_1_eq, comparator_1_gt, comparator_1_lt, DC_JUMP, EXT_p5, EXT_p6, IMMED_OE, IRQ_OE,
       not_1_out, not_2_out, RAM_OE, RAM_WE, RF_HWE, RF_LWE, RF_SFR, RFSRCR_WE, ROM_OE, SFR_OE, SR_WE, WR_WE,
       XRAM_OE;
  wire [2:0] BR_SRC, BUS_SRC, JUMP_TYPE;
  wire [3:0] ALUSD_FUNC, multiplexer_2_out, RF_SRC;
  wire [5:4] multiplexer_2_out_2;
  wire [6:0] and_2_out;
  wire [7:0] DBUS, IMMED, RF_Q;
  wire [7:4] RFSRCR_q;
  wire [11:0] ADDRESS, dcouter_1_q;
  wire [15:0] SR_q;
  wire [47:44] DECODER_2_d;

  Decoder #(.Selector_Bits(3)) decoder_1 (
    .sel(BUS_SRC), .out_0(ALUS_OE), .out_1(ALUDL_OE), .out_2(ALUDH_OE), .out_3(IMMED_OE), .out_4(RAM_OE),
    .out_5(XRAM_OE), .out_6(ROM_OE), .out_7(IRQ_OE));
  DCOUTER #(.generic("Bits := 12;")) dcouter_1 (
    .CLK(CLK_t), .nCLR(CLR), .CNT(1'b1), .nLE(DC_JUMP), .D(ADDRESS), .Q(dcouter_1_q));
  Comparator #(.Bits(8)) comparator_1 (
    .a(RF_Q), .b(IMMED), .gt(comparator_1_gt), .eq(comparator_1_eq), .lt(comparator_1_lt));
  // Probe on dcouter_1_q
  Multiplexer #(.Selector_Bits(3)) multiplexer_1 (
    .sel(JUMP_TYPE), .in_0(1'b0), .in_1(1'b1), .in_2(comparator_1_gt), .in_3(comparator_1_eq),
    .in_4(comparator_1_lt), .in_5(BR_Q), .in_6(RST), .in_7(1'b0), .out(DC_JUMP));
  ROM #(.AddrBits(12), .Bits(48)) DECODER_2 (
    .A(dcouter_1_q), .sel(1'b1),
    .D({DECODER_2_d, IMMED, ADDRESS, JUMP_TYPE, ALUSD_FUNC, RAM_WE, RFSRCR_WE, BR_SRC, SR_WE, WR_WE, BUS_SRC, RF_SFR, RF_HWE, RF_LWE, RF_SRC}));
  Register #(.Bits(8)) RFSRCR (.D(DBUS), .C(CLK_t), .en(RFSRCR_WE), .Q({RFSRCR_q, and_2_out[3:0]}));
  and and_1 (and_2_out[5], RFSRCR_q[4], RAM_WE);
  and and_2 (and_2_out[6], RFSRCR_q[4], RAM_OE);
  Multiplexer #(.Bits(7)) multiplexer_2 (
    .sel(RF_SFR), .in_0({1'b0, RF_HWE, RF_LWE, RF_SRC}),
    .in_1({and_2_out[6:5], and_2_out[5], and_2_out[3:0]}),
    .out({SFR_OE, multiplexer_2_out_2, multiplexer_2_out}));
  // Probe on RF_SRC
  // Probe on RF_LWE
  // Probe on RF_HWE
  // Probe on RF_SFR
  // Probe on BUS_SRC
  // Probe on WR_WE
  // Probe on SR_WE
  // Probe on BR_SRC
  // Probe on RFSRCR_WE
  // Probe on RAM_WE
  // Probe on ALUSD_FUNC
  // Probe on JUMP_TYPE
  // Probe on ADDRESS
  // Probe on IMMED
  Button button_1 (.out(button_1_out));
  PullDown #(.Bits(8)) pulldown_1 (.out(DBUS));
  reg_file RF (
    .CLK(CLK_t), .RS(multiplexer_2_out), .D(DBUS), .LLE(multiplexer_2_out_2[4]),
    .HLE(multiplexer_2_out_2[5]), .Q(RF_Q));
  BR BR (.CLK(CLK_t), .CLR(CLR), .S(BR_SRC), .ALUDF(ALUD_CO), .ALUSF(ALUD_CO), .A0(RF_Q[0]), .A7(RF_Q[7]), .Q(BR_Q));
  // SwitchDT switchdt_1: pin names not known; wires that end beside it: clk, button_1_out, CLKR
  // Probe on DBUS
  // Probe on RF_Q
  reg__sync_clear #(.generic("Bits := 8;")) WR (.D(DBUS), .CLK(CLK_t), .CLR(CLR), .nLE(WR_WE), .Q(SR_q[7:0]));
  reg__sync_clear #(.generic("Bits := 8;")) SR (.D(DBUS), .CLK(CLK_t), .CLR(CLR), .nLE(SR_WE), .Q(SR_q[15:8]));
  assign DBUS = SFR_OE ? RF_Q : 8'bz;  // Driver driver_1
  // Probe on SR_q[7:0]
  // Probe on SR_q[15:8]
  and and_3 (and_3_out, RAM_WE, CLK_t, not_1_out);
  not not_1 (not_1_out, CLK_t);
  ALU ALU (
    .A(RF_Q), .B(SR_q[7:0]), .S(ALUSD_FUNC), .CI(BR_Q), .nSOE(ALUS_OE), .nDLOE(ALUDL_OE), .nDHOE(ALUDH_OE),
    .O(DBUS), .CO(ALUD_CO));
  // Probe on SR_q
  ROM #(.AddrBits(16), .isProgramMemory("true"), .Bits(8)) ROM (.A(SR_q), .sel(ROM_OE), .D(DBUS));
  ASSERT ASSERT (.C(CLK_t), .D(DBUS), .A(SR_q[15:8]), .WE(RAM_WE), .F(ASSERT_f));
  RAMSinglePortSel #(.AddrBits(7), .isProgramMemory("true"), .Bits(8)) RAM (
    .A(SR_q[14:8]), .CS(not_2_out), .WE(and_3_out), .OE(RAM_OE), .D(DBUS));
  not not_2 (not_2_out, SR_q[15]);
  assign DBUS = IMMED_OE ? IMMED : 8'bz;  // Driver driver_2
  // EXTCTL EXT: pin names not known; wires that end beside it: RAM_WE, SR_q[15:8], DBUS, CLK_t, EXT_p5, EXT_p6
  STALL stall_1 (.C(CLKR), .S(ASSERT_f), .G(in_4), .O(CLK_t));
  // Probe on EXT_p5
  // Probe on EXT_p6

  // Other names for the same wires on the sheet: GO = in_4

  // Notes on the sheet:
  //   clk: Hz: 2147483647
  //   contents of DECODER_2 (hex, n*v repeats v):
  //   127c80488,80889,33a,85106,1a3135,1e54b8,1e08b9,8007e80000a,c004480000a,e002580000a,
  //   f001680000a,f801080040a,a00bc,80485,1a088c,236,f401380000a,f601280000a,f501380000a,
  //   f201580000a,f301580000a,f101680000a,e801e80000a,ec01b80000a,ee01a80000a,ef01a80000a,
  //   ed01b80000a,ea01d80000a,eb01d80000a,e901e80000a,e402280000a,e602180000a,e702180000a,
  //   e502280000a,e202480000a,e302480000a,e102580000a,d003580000a,d802e80000a,dc02b80000a,
  //   de02a80000a,df02a80000a,dd02b80000a,da02d80000a,db02d80000a,d902e80000a,d403280000a,
  //   d603180000a,d703180000a,d503280000a,d203480000a,d303480000a,d103580000a,c803d80000a,
  //   cc03a80000a,ce03980000a,cf03980000a,cd03a80000a,ca03c80000a,cb03c80000a,c903d80000a,
  //   c404180000a,c604080000a,c704080000a,c504180000a,c204380000a,c304380000a,c104480000a,
  //   a006780000a,b005580000a,b804e80000a,bc04b80000a,be04a80000a,bf04a80000a,bd04b80000a,
  //   ba04d80000a,bb04d80000a,b904e80000a,b405280000a,b605180000a,b705180000a,b505280000a,
  //   b205480000a,b305480000a,b105580000a,a805d80000a,ac05a80000a,ae05980000a,af05980000a,
  //   ad05a80000a,aa05c80000a,ab05c80000a,a905d80000a,a406180000a,a606080000a,a706080000a,
  //   a506180000a,a206680000a,a306680000a,3580,450b1,10f2400b2,a106780000a,9006f80000a,
  //   9806980000a,9406c80000a,9606b80000a,9506c80000a,9206e80000a,9306e80000a,9106f80000a,
  //   8807780000a,8c07480000a,8e07380000a,8f07380000a,8d07480000a,8a07680000a,8b07680000a,
  //   8907780000a,8407b80000a,8607a80000a,8707a80000a,8507b80000a,8207d80000a,8307d80000a,
  //   8107e80000a,400cd80000a,600ae80000a,7009f80000a,7808980000a,7c08680000a,7e08580000a,
  //   7f08580000a,7d08680000a,7a08880000a,7b08880000a,7908980000a,7409c80000a,7608c80000a,
  //   7708c80000a,7509680000a,333c,1e54b8,408b9,700,6800c,8088c,b30c0,1e50b8,10f3e00b9,
  //   80488,80889,336,3580,450b8,10f2400b9,7209e80000a,7309e80000a,7109f80000a,680a780000a,
  //   6c0a480000a,6e0a380000a,6f0a380000a,6d0a480000a,6a0a680000a,6b0a680000a,690a780000a,
  //   640ab80000a,660aa80000a,670aa80000a,650ab80000a,620ad80000a,630ad80000a,610ae80000a,
  //   500be80000a,580b780000a,5c0b480000a,5e0b380000a,5f0b380000a,5d0b480000a,5a0b680000a,
  //   5b0b680000a,590b780000a,540bb80000a,560ba80000a,570ba80000a,550bb80000a,520bd80000a,
  //   530bd80000a,510be80000a,480c680000a,4c0c380000a,4e0c280000a,4f0c280000a,4d0c380000a,
  //   4a0c580000a,4b0c580000a,490c680000a,440ca80000a,460c980000a,470c980000a,450ca80000a,
  //   420cc80000a,430cc80000a,410cd80000a,200ed80000a,300de80000a,380d780000a,3c0d480000a,
  //   3e0d380000a,3f0d380000a,3d0d480000a,3a0d680000a,3b0d680000a,390d780000a,340db80000a,
  //   360da80000a,370da80000a,350db80000a,320dd80000a,330dd80000a,310de80000a,280e680000a,
  //   2c0e380000a,2e0e280000a,2f0e280000a,2d0e380000a,2a0e580000a,2b0e580000a,290e680000a,
  //   240ea80000a,260e980000a,270e980000a,250ea80000a,220ec80000a,230ec80000a,210ed80000a,
  //   100fd80000a,180f680000a,1c0f380000a,1e0f280000a,1f0f280000a,1d0f380000a,1a0f580000a,
  //   1b0f580000a,190f680000a,140fa80000a,160f980000a,170f980000a,150fa80000a,120fc80000a,
  //   130fc80000a,110fd80000a,810580000a,c10280000a,e10180000a,f10180000a,d10280000a,a10480000a,
  //   b10480000a,910580000a,410a80000a,610880000a,710880000a,510980000a,100036,210d80000a,
  //   310d80000a,80036,110f80000a,10f200000,80000880483,3bc,e04bc,100080000c,80484,1600bc,
  //   8048b,a00bd,a00be,80484,16348d,6508c,a00000,10048c,e00be,40000e,c00bb,100830,90088,
  //   100830,90089,2043c,1b9,2a00b8,1b6,1b7,1b0,1b5,1b1,1b2,1b3,1b4,1b8,1b9,1ba,127c001bb,
  //   200000
  //   contents of ROM (hex, n*v repeats v):
  //   75,0,0,75,1,1,75,2,2,75,3,3,75,4,4,75,5,5,75,6,6,75,7,7,75,8,8,75,9,9,75,a,a,75,b,
  //   b,75,c,c,75,d,d,75,e,e,75,f,f,75,10,10,75,11,11,75,12,12,75,13,13,75,14,14,75,15,
  //   15,75,16,16,75,17,17,75,18,18,75,19,19,75,1a,1a,75,1b,1b,75,1c,1c,75,1d,1d,75,1e,
  //   1e,75,1f,1f,75,20,20,75,21,21,75,22,22,75,23,23,75,24,24,75,25,25,75,26,26,75,27,
  //   27,75,28,28,75,29,29,75,2a,2a,75,2b,2b,75,2c,2c,75,2d,2d,75,2e,2e,75,2f,2f,75,30,
  //   30,75,31,31,75,32,32,75,33,33,75,34,34,75,35,35,75,36,36,75,37,37,75,38,38,75,39,
  //   39,75,3a,3a,75,3b,3b,75,3c,3c,75,3d,3d,75,3e,3e,75,3f,3f,75,40,40,75,41,41,75,42,
  //   42,75,43,43,75,44,44,75,45,45,75,46,46,75,47,47,75,48,48,75,49,49,75,4a,4a,75,4b,
  //   4b,75,4c,4c,75,4d,4d,75,4e,4e,75,4f,4f,75,50,50,75,51,51,75,52,52,75,53,53,75,54,
  //   54,75,55,55,75,56,56,75,57,57,75,58,58,75,59,59,75,5a,5a,75,5b,5b,75,5c,5c,75,5d,
  //   5d,75,5e,5e,75,5f,5f,75,60,60,75,61,61,75,62,62,75,63,63,75,64,64,75,65,65,75,66,
  //   66,75,67,67,75,68,68,75,69,69,75,6a,6a,75,6b,6b,75,6c,6c,75,6d,6d,75,6e,6e,75,6f,
  //   6f,75,70,70,75,71,71,75,72,72,75,73,73,75,74,74,75,75,75,75,76,76,75,77,77,75,78,
  //   78,75,79,79,75,7a,7a,75,7b,7b,75,7c,7c,75,7d,7d,75,7e,7e,75,7f,7f,75,81,81,75,82,
  //   82,75,83,83,75,a8,a8,75,b8,b8,75,d0,d0,75,e0,e0,75,f0,f0,75,ef,0,75,ee,1
endmodule
